// Logisim project P4_CPU_referenceCircuit.circ as structural Verilog: 12 circuits, main circuit PCmodule_2
// PC
module PCmodule_2 (
  input  clk,
  input  reset,
  input  [31:0] nextPC,
  output [31:0] currentPC
);

  wire [31:0] register_1_q, subtractor_1_out;

  Subtractor #(.width(32)) subtractor_1 (.a(nextPC), .b(32'h3000), .out(subtractor_1_out));  // open: bin, bout
  Register #(.width(32)) register_1 (.D(subtractor_1_out), .Q(register_1_q), .clk(clk), .clr(reset));  // open: en
  Adder #(.width(32)) adder_1 (.a(register_1_q), .b(32'h3000), .out(currentPC));  // open: cin, cout

  // Notes on the sheet:
  //   Input
  //   PC
  //   Output
endmodule

// NPC
module NPCmodule_2 (
  input  [31:0] currentPC,
  input  [15:0] beq_imm16,
  input  [25:0] jar_imm26,
  input  [31:0] jr_A32,
  input  [1:0] NPCop,
  input  beq_zero,
  output [31:0] nextPC
);

  wire [31:0] beq_imm32, beq_imm32_add, beqPC, bit_extender_1_out, sequentialPC;

  Adder #(.width(32)) adder_1 (.a(currentPC), .b(32'h4), .out(sequentialPC));  // open: cin, cout
  assign bit_extender_1_out = {{16{beq_imm16[15]}}, beq_imm16};  // Bit_Extender bit_extender_1
  Adder #(.width(32)) adder_2 (.a(sequentialPC), .b(beq_imm32_add), .out(beqPC));  // open: cin, cout
  Shifter #(.width(32)) shifter_1 (.in(bit_extender_1_out), .\dist (5'b00010), .out(beq_imm32));
  Multiplexer #(.width(32)) multiplexer_1 (
    .in0({32{1'b0}}), .in1(beq_imm32), .out(beq_imm32_add), .sel(beq_zero));  // open: en
  // Probe on sequentialPC
  // Probe on beq_imm32
  // Probe on beq_imm32_add
  // Probe on beqPC
  Multiplexer #(.select(2), .width(32)) multiplexer_2 (
    .in0(sequentialPC), .in1(beqPC), .in2({32{1'b0}}), .in3({32{1'b0}}), .out(nextPC), .sel(NPCop));  // open: en

  // Notes on the sheet:
  //   Input
  //   calculate
  //   the calculate of NPCop
  //   op==00 sequential
  //   op==01 beq
  //   op==10 jar
  //   op==11 jr
  //   留给jar和j的接口
  //   select
  //   Output
endmodule

// IM
module IMmodule_2 (
  input  [31:0] currentPC,
  output [31:0] instruction
);

  wire [11:0] currentIM;
  wire [31:30] subtractor_1_out;

  Subtractor #(.width(32)) subtractor_1 (
    .a(currentPC), .b(32'h3000),
    .out({subtractor_1_out, subtractor_1_out, subtractor_1_out, subtractor_1_out, subtractor_1_out, subtractor_1_out, subtractor_1_out, subtractor_1_out, subtractor_1_out, currentIM, subtractor_1_out}));  // open: bin, bout
  ROM #(.addrWidth(12), .dataWidth(32)) rom_1 (.addr(currentIM), .data(instruction));  // open: sel
  // also tied to GND on the sheet: {subtractor_1_out[30], subtractor_1_out[31]}

  // Notes on the sheet:
  //   input
  //   Output
  //   Retrieve the instruction
  //   contents of rom_1 (hex, n*v repeats v):
  //   341c0000 341d0000 34013456 210820 8c010004 ac010004 3c027878 411822 3c051234 34040005 0 ac85ffff
  //   8c83ffff 10650001 1000000d 34670404 10e3000b 0 3c087777 3508ffff 80022 34001100 e65020 34080000
  //   34090001 340a0001 10a4020 1109fffe 1000ffff
endmodule

// IFU
module IFUmodule_1 (
  input  clk,
  input  reset,
  input  [15:0] beq_imm16,
  input  [1:0] NPCop,
  input  beq_zero,
  output [31:0] currentPC,
  output [31:0] instruction
);

  wire [31:0] nextPC;

  PCmodule_2 PC (.clk(clk), .reset(reset), .nextPC(nextPC), .currentPC(currentPC));
  NPCmodule_2 npcmodule_2_1 (
    .currentPC(currentPC), .beq_imm16(beq_imm16), .NPCop(NPCop), .beq_zero(beq_zero), .nextPC(nextPC));  // open: jar_imm26, jr_A32
  IMmodule_2 immodule_2_1 (.currentPC(currentPC), .instruction(instruction));

  // Notes on the sheet:
  //   Input
  //   Output
  //   Instruction Fetch Unit
  //   jar and j
  //   beq_zero信号由ALU给出
  //   zero==0 beq不跳转
  //   zero==1 beq跳转
endmodule

// Splittter
module Splittermodule_1 (
  input  [31:0] instruction,
  output [5:0] opcode,
  output [4:0] rs_5,
  output [4:0] rt_5,
  output [4:0] rd_5,
  output [4:0] shamt,
  output [5:0] funct,
  output [15:0] imm16,
  output [25:0] imm26
);


  assign funct = instruction[5:0];
  assign imm16 = instruction[15:0];
  assign imm26 = instruction[25:0];
  assign opcode = instruction[31:26];
  assign rd_5 = instruction[15:11];
  assign rs_5 = instruction[25:21];
  assign rt_5 = instruction[20:16];
  assign shamt = instruction[10:6];

  // Notes on the sheet:
  //   Input
  //   Splitter
  //   Output
endmodule

// GRF
module GRFmodule_1 (
  input  clk,
  input  reset,
  input  GRFop,
  input  [4:0] rs_5,
  input  [4:0] rt_5,
  input  [4:0] rd_5,
  input  [31:0] WD,
  output [31:0] RD1,
  output [31:0] RD2
);

  wire C1, C2, C3, C4, C5, C6, C7, C8, C9, C10, C11, C12, C13, C14, C15, C16, C17, C18, C19, C20, C21, C22,
       C23, C24, C25, C26, C27, C28, C29, c30, c31, pull_resistor_2_node;
  wire [31:0] _00, _01, _01in, _02, _02in, _03, _03in, _04, _04in, _05, _05in, _06, _06in, _07, _07in, _08,
       _08in, _09, _09in, _10, _10in, _11, _11in, _12, _12in, _13, _13in, _14, _14in, _15, _15in, _16, _16in,
       _17, _17in, _18, _18in, _19, _19in, _20, _20in, _21, _21in, _22, _22in, _23, _23in, _24, _24in, _25,
       _25in, _26, _26in, _27, _27in, _28, _28in, _29, _29in, _30, _30in, _31, _31in, pull_resistor_1_node;

  Demultiplexer #(.select(5), .width(32)) demultiplexer_1 (
    .out1(_01in), .out2(_02in), .out3(_03in), .out4(_04in), .out5(_05in), .out6(_06in), .out7(_07in),
    .out8(_08in), .out9(_09in), .out10(_10in), .out11(_11in), .out12(_12in), .out13(_13in), .out14(_14in),
    .out15(_15in), .out16(_16in), .out17(_17in), .out18(_18in), .out19(_19in), .out20(_20in), .out21(_21in),
    .out22(_22in), .out23(_23in), .out24(_24in), .out25(_25in), .out26(_26in), .out27(_27in), .out28(_28in),
    .out29(_29in), .out30(_30in), .out31(_31in), .in(WD), .sel(rd_5), .en(GRFop));  // open: out0
  Pull_Resistor pull_resistor_1 (.node(pull_resistor_1_node));
  Register #(.width(32)) u__00 (.D(pull_resistor_1_node), .en(GRFop), .Q(_00), .clk(clk), .clr(reset));
  Register #(.width(32)) u__08 (.D(_08in), .en(C8), .Q(_08), .clk(clk), .clr(reset));
  Register #(.width(32)) u__16 (.D(_16in), .en(C16), .Q(_16), .clk(clk), .clr(reset));
  Register #(.width(32)) u__24 (.D(_24in), .en(C24), .Q(_24), .clk(clk), .clr(reset));
  comparator_2 comparator_2_1 (.A3(rd_5), .c(5'b01000), .WE(GRFop), .out_4(C8));
  comparator_2 comparator_2_2 (.A3(rd_5), .c(5'b10000), .WE(GRFop), .out_4(C16));
  comparator_2 comparator_2_3 (.A3(rd_5), .c(5'b11000), .WE(GRFop), .out_4(C24));
  Register #(.width(32)) u__01 (.D(_01in), .en(C1), .Q(_01), .clk(clk), .clr(reset));
  Register #(.width(32)) u__09 (.D(_09in), .en(C9), .Q(_09), .clk(clk), .clr(reset));
  Register #(.width(32)) u__17 (.D(_17in), .en(C17), .Q(_17), .clk(clk), .clr(reset));
  Register #(.width(32)) u__25 (.D(_25in), .en(C25), .Q(_25), .clk(clk), .clr(reset));
  comparator_2 comparator_2_4 (.A3(rd_5), .c(5'b00001), .WE(GRFop), .out_4(C1));
  comparator_2 comparator_2_5 (.A3(rd_5), .c(5'b01001), .WE(GRFop), .out_4(C9));
  comparator_2 comparator_2_6 (.A3(rd_5), .c(5'b10001), .WE(GRFop), .out_4(C17));
  comparator_2 comparator_2_7 (.A3(rd_5), .c(5'b11001), .WE(GRFop), .out_4(C25));
  Register #(.width(32)) u__02 (.D(_02in), .en(C2), .Q(_02), .clk(clk), .clr(reset));
  Register #(.width(32)) u__10 (.D(_10in), .en(C10), .Q(_10), .clk(clk), .clr(reset));
  Register #(.width(32)) u__18 (.D(_18in), .en(C18), .Q(_18), .clk(clk), .clr(reset));
  Register #(.width(32)) u__26 (.D(_26in), .en(C26), .Q(_26), .clk(clk), .clr(reset));
  comparator_2 comparator_2_8 (.A3(rd_5), .c(5'b00010), .WE(GRFop), .out_4(C2));
  comparator_2 comparator_2_9 (.A3(rd_5), .c(5'b01010), .WE(GRFop), .out_4(C10));
  comparator_2 comparator_2_10 (.A3(rd_5), .c(5'b10010), .WE(GRFop), .out_4(C18));
  comparator_2 comparator_2_11 (.A3(rd_5), .c(5'b11010), .WE(GRFop), .out_4(C26));
  Register #(.width(32)) u__03 (.D(_03in), .en(C3), .Q(_03), .clk(clk), .clr(reset));
  Register #(.width(32)) u__11 (.D(_11in), .en(C11), .Q(_11), .clk(clk), .clr(reset));
  Register #(.width(32)) u__19 (.D(_19in), .en(C19), .Q(_19), .clk(clk), .clr(reset));
  Register #(.width(32)) u__27 (.D(_27in), .en(C27), .Q(_27), .clk(clk), .clr(reset));
  comparator_2 comparator_2_12 (.A3(rd_5), .c(5'b00011), .WE(GRFop), .out_4(C3));
  comparator_2 comparator_2_13 (.A3(rd_5), .c(5'b01011), .WE(GRFop), .out_4(C11));
  comparator_2 comparator_2_14 (.A3(rd_5), .c(5'b10011), .WE(GRFop), .out_4(C19));
  comparator_2 comparator_2_15 (.A3(rd_5), .c(5'b11011), .WE(GRFop), .out_4(C27));
  Register #(.width(32)) u__04 (.D(_04in), .en(C4), .Q(_04), .clk(clk), .clr(reset));
  Register #(.width(32)) u__12 (.D(_12in), .en(C12), .Q(_12), .clk(clk), .clr(reset));
  Register #(.width(32)) u__20 (.D(_20in), .en(C20), .Q(_20), .clk(clk), .clr(reset));
  Register #(.width(32)) u__28 (.D(_28in), .en(C28), .Q(_28), .clk(clk), .clr(reset));
  comparator_2 comparator_2_16 (.A3(rd_5), .c(5'b00100), .WE(GRFop), .out_4(C4));
  comparator_2 comparator_2_17 (.A3(rd_5), .c(5'b01100), .WE(GRFop), .out_4(C12));
  comparator_2 comparator_2_18 (.A3(rd_5), .c(5'b10100), .WE(GRFop), .out_4(C20));
  comparator_2 comparator_2_19 (.A3(rd_5), .c(5'b11100), .WE(GRFop), .out_4(C28));
  Register #(.width(32)) u__05 (.D(_05in), .en(C5), .Q(_05), .clk(clk), .clr(reset));
  Register #(.width(32)) u__13 (.D(_13in), .en(C13), .Q(_13), .clk(clk), .clr(reset));
  Register #(.width(32)) u__21 (.D(_21in), .en(C21), .Q(_21), .clk(clk), .clr(reset));
  Register #(.width(32)) u__29 (.D(_29in), .en(C29), .Q(_29), .clk(clk), .clr(reset));
  comparator_2 comparator_2_20 (.A3(rd_5), .c(5'b00101), .WE(GRFop), .out_4(C5));
  comparator_2 comparator_2_21 (.A3(rd_5), .c(5'b01101), .WE(GRFop), .out_4(C13));
  comparator_2 comparator_2_22 (.A3(rd_5), .c(5'b10101), .WE(GRFop), .out_4(C21));
  comparator_2 comparator_2_23 (.A3(rd_5), .c(5'b11101), .WE(GRFop), .out_4(C29));
  Register #(.width(32)) u__06 (.D(_06in), .en(C6), .Q(_06), .clk(clk), .clr(reset));
  Register #(.width(32)) u__14 (.D(_14in), .en(C14), .Q(_14), .clk(clk), .clr(reset));
  Register #(.width(32)) u__22 (.D(_22in), .en(C22), .Q(_22), .clk(clk), .clr(reset));
  Register #(.width(32)) u__30 (.D(_30in), .en(c30), .Q(_30), .clk(clk), .clr(reset));
  comparator_2 comparator_2_24 (.A3(rd_5), .c(5'b00110), .WE(GRFop), .out_4(C6));
  comparator_2 comparator_2_25 (.A3(rd_5), .c(5'b01110), .WE(GRFop), .out_4(C14));
  comparator_2 comparator_2_26 (.A3(rd_5), .c(5'b10110), .WE(GRFop), .out_4(C22));
  comparator_2 comparator_2_27 (.A3(rd_5), .c(5'b11110), .WE(GRFop), .out_4(c30));
  Register #(.width(32)) u__07 (.D(_07in), .en(C7), .Q(_07), .clk(clk), .clr(reset));
  Register #(.width(32)) u__15 (.D(_15in), .en(C15), .Q(_15), .clk(clk), .clr(reset));
  Register #(.width(32)) u__23 (.D(_23in), .en(C23), .Q(_23), .clk(clk), .clr(reset));
  Register #(.width(32)) u__31 (.D(_31in), .en(c31), .Q(_31), .clk(clk), .clr(reset));
  comparator_2 comparator_2_28 (.A3(rd_5), .c(5'b00111), .WE(GRFop), .out_4(C7));
  comparator_2 comparator_2_29 (.A3(rd_5), .c(5'b01111), .WE(GRFop), .out_4(C15));
  comparator_2 comparator_2_30 (.A3(rd_5), .c(5'b10111), .WE(GRFop), .out_4(C23));
  comparator_2 comparator_2_31 (.A3(rd_5), .c({5{1'b1}}), .WE(GRFop), .out_4(c31));
  Multiplexer #(.select(5), .width(32)) multiplexer_1 (
    .in0(_00), .in1(_01), .in2(_02), .in3(_03), .in4(_04), .in5(_05), .in6(_06), .in7(_07), .in8(_08),
    .in9(_09), .in10(_10), .in11(_11), .in12(_12), .in13(_13), .in14(_14), .in15(_15), .in16(_16),
    .in17(_17), .in18(_18), .in19(_19), .in20(_20), .in21(_21), .in22(_22), .in23(_23), .in24(_24),
    .in25(_25), .in26(_26), .in27(_27), .in28(_28), .in29(_29), .in30(_30), .in31(_31), .out(RD1),
    .sel(rs_5), .en(pull_resistor_2_node));
  Multiplexer #(.select(5), .width(32)) multiplexer_2 (
    .in0(_00), .in1(_01), .in2(_02), .in3(_03), .in4(_04), .in5(_05), .in6(_06), .in7(_07), .in8(_08),
    .in9(_09), .in10(_10), .in11(_11), .in12(_12), .in13(_13), .in14(_14), .in15(_15), .in16(_16),
    .in17(_17), .in18(_18), .in19(_19), .in20(_20), .in21(_21), .in22(_22), .in23(_23), .in24(_24),
    .in25(_25), .in26(_26), .in27(_27), .in28(_28), .in29(_29), .in30(_30), .in31(_31), .out(RD2),
    .sel(rt_5), .en(pull_resistor_2_node));
  Pull_Resistor #(.pull(1)) pull_resistor_2 (.node(pull_resistor_2_node));

  // Other names for the same wires on the sheet: A1[4:0] = rs_5; A2[4:0] = rt_5; A3[4:0] = rd_5
endmodule

module comparator_2 (
  input  [4:0] A3,
  input  [4:0] c,
  input  WE,
  output out_4
);

  wire comparator_1_eq;

  Comparator #(.width(5), .mode("unsigned")) comparator_1 (.a(A3), .b(c), .eq(comparator_1_eq));  // open: gt, lt
  and and_1 (out_4, comparator_1_eq, WE);
endmodule

// ALU
module ALUmodule_1 (
  input  [1:0] ALUop,
  input  [31:0] memory_rs,
  input  [31:0] memory_rt,
  output zero,
  output [31:0] ANS
);

  wire [31:0] ADD, LUI, OR, SUB;

  Adder #(.width(32)) adder_1 (.a(memory_rs), .b(memory_rt), .out(ADD));  // open: cin, cout
  Subtractor #(.width(32)) subtractor_1 (.a(memory_rs), .b(memory_rt), .out(SUB));  // open: bin, bout
  assign OR = memory_rs | memory_rt;  // OR_Gate or_1, 32 bits wide
  Shifter #(.width(32)) shifter_1 (.in(memory_rt), .\dist (5'b10000), .out(LUI));
  Comparator #(.width(32), .mode("unsigned")) comparator_1 (.a(memory_rs), .b(memory_rt), .eq(zero));  // open: gt, lt
  // Probe on ADD
  // Probe on SUB
  // Probe on OR
  // Probe on LUI
  // Probe on zero
  Multiplexer #(.select(2), .width(32)) multiplexer_1 (
    .in0(ADD), .in1(SUB), .in2(OR), .in3(LUI), .out(ANS), .sel(ALUop));  // open: en
  // Probe on ANS

  // Notes on the sheet:
  //   Input
  //   ALU
  //   Output
endmodule

// DM
module DMmodule_1 (
  input  DMop,
  input  [31:0] address,
  input  [31:0] DataInput,
  input  clk,
  input  reset,
  output [31:0] DataOutput
);

  RAM #(.addrWidth(12), .dataWidth(32), .bus("separate")) ram_1 (
    .addr(address[13:2]), .din(DataInput), .data(DataOutput), .str(DMop), .clk(clk), .clr(reset));  // open: sel, ld

  assign {address[29:14], address[1:0]} = {address[31:30], address[31:30], address[31:30], address[31:30], address[31:30], address[31:30], address[31:30], address[31:30], address[31:30]};
  // also tied to GND on the sheet: {address[30], address[31]}

  // Other names for the same wires on the sheet: address12[11:0] = address[13:2]; op = DMop

  // Notes on the sheet:
  //   Input
  //   Address
  //   access memory
  //   Output
endmodule

module EXTmodule_1 (
  input  [1:0] EXTop,
  input  [15:0] imm16,
  input  [25:0] imm26,
  output [31:0] Output
);

  wire [31:0] _16signEXT, _16zeroEXT, _26signEXT, _26zeroEXT;

  assign _16zeroEXT = {{16{1'b0}}, imm16};  // Bit_Extender bit_extender_1
  assign _16signEXT = {{16{imm16[15]}}, imm16};  // Bit_Extender bit_extender_2
  assign _26zeroEXT = {{6{1'b0}}, imm26};  // Bit_Extender bit_extender_3
  assign _26signEXT = {{6{imm26[25]}}, imm26};  // Bit_Extender bit_extender_4
  Multiplexer #(.select(2), .width(32)) multiplexer_1 (
    .in0(_16zeroEXT), .in1(_16signEXT), .in2(_26zeroEXT), .in3(_26signEXT), .out(Output), .sel(EXTop));  // open: en

  // Other names for the same wires on the sheet: ANS[31:0] = Output; op[1:0] = EXTop

  // Notes on the sheet:
  //   Input
  //   Extend
  //   EXTop扩展选择码
  //   op==00 16位零扩展
  //   op==01 16位符号扩展
  //   op==10 26位零扩展
  //   op==11 26位符号扩展
endmodule

module Controlmodule_1 (
  input  [5:0] opcode,
  input  [5:0] funct,
  output [1:0] NPCop,
  output GRFop,
  output AddSub,
  output write,
  output [1:0] ALUop,
  output IMMop,
  output DMop,
  output [1:0] EXTop
);

  wire ADD, LUI, not_1_out, not_2_out, not_3_out, not_4_out, not_5_out, not_6_out, not_7_out, not_8_out,
       not_9_out, not_10_out, not_11_out, not_12_out, ORI, SUB;

  not not_1 (not_1_out, opcode[5]);
  not not_2 (not_2_out, opcode[4]);
  not not_3 (not_3_out, opcode[2]);
  not not_4 (not_4_out, opcode[3]);
  not not_5 (not_5_out, opcode[1]);
  not not_6 (not_6_out, opcode[0]);
  not not_7 (not_7_out, funct[5]);
  not not_8 (not_8_out, funct[1]);
  not not_9 (not_9_out, funct[3]);
  not not_10 (not_10_out, funct[4]);
  not not_11 (not_11_out, funct[2]);
  not not_12 (not_12_out, funct[0]);
  and u_ADD (ADD, not_12_out, not_8_out, not_11_out, not_9_out, not_10_out, funct[5], not_6_out, not_5_out, not_3_out, not_4_out, not_2_out, not_1_out);
  and u_SUB (SUB, not_12_out, funct[1], not_11_out, not_9_out, not_10_out, funct[5], not_6_out, not_5_out, not_3_out, not_4_out, not_2_out, not_1_out);
  and u_ORI (ORI, opcode[0], not_5_out, opcode[2], opcode[3], not_2_out, not_1_out);
  and LW (write, opcode[0], opcode[1], not_3_out, not_4_out, not_2_out, opcode[5]);
  and SW (DMop, opcode[0], opcode[1], not_3_out, opcode[3], not_2_out, opcode[5]);
  and BEQ (NPCop[0], not_6_out, not_5_out, opcode[2], not_4_out, not_2_out, not_1_out);
  and u_LUI (LUI, opcode[0], opcode[1], opcode[2], opcode[3], not_2_out, not_1_out);
  or or_1 (GRFop, ADD, SUB, ORI, write, LUI);
  or or_2 (AddSub, ADD, SUB);
  or or_3 (ALUop[1], ORI, LUI);
  or or_4 (ALUop[0], SUB, LUI);
  or or_5 (IMMop, ORI, write, DMop, LUI);
  or or_6 (EXTop[0], write, DMop);

  assign EXTop[1] = 1'b0;
  assign NPCop[1] = 1'b0;

  // Other names for the same wires on the sheet: f0 = funct[0]; f1 = funct[1]; f2 = funct[2]; f3 = funct[3];
  //   f4 = funct[4]; f5 = funct[5]; LW = write; BEQ = NPCop[0]; op0 = opcode[0]; op1 = opcode[1]; op2 = opcode[2];
  //   op3 = opcode[3]; op4 = opcode[4]; op5 = opcode[5]; SW = DMop

  // Notes on the sheet:
  //   Input
  //   Control
  //   Output
endmodule

module main (
  input  reset,
  output [31:0] Instr,
  output [31:0] PC,
  output RegWrite,
  output [4:0] RegAddr,
  output [31:0] RegData,
  output MemWrite,
  output [31:0] MemAddr,
  output [31:0] MemData
);

  wire AddSub, clk, IMMop, write, zero;
  wire [1:0] ALUop, EXTop, NPCop;
  wire [4:0] multiplexer_1_out, rd, rs, rt, shamt;
  wire [5:0] funct, opcode;
  wire [15:0] imm16;
  wire [31:0] DataOutput, EXT32, multiplexer_2_out, multiplexer_3_out, RD1;

  Clock u_clk (.out(clk));
  IFUmodule_1 ifumodule_1_1 (
    .clk(clk), .reset(reset), .beq_imm16(imm16), .NPCop(NPCop), .beq_zero(zero), .instruction(Instr),
    .currentPC(PC));
  Splittermodule_1 splittermodule_1_1 (
    .instruction(Instr), .opcode(opcode), .rs_5(rs), .rt_5(rt), .rd_5(rd), .shamt(shamt), .funct(funct),
    .imm16(imm16));  // open: imm26
  Controlmodule_1 controlmodule_1_1 (
    .opcode(opcode), .funct(funct), .NPCop(NPCop), .GRFop(RegWrite), .AddSub(AddSub), .write(write),
    .ALUop(ALUop), .IMMop(IMMop), .DMop(MemWrite), .EXTop(EXTop));
  Multiplexer #(.width(5)) multiplexer_1 (.in0(rt), .in1(rd), .out(multiplexer_1_out), .sel(AddSub));  // open: en
  Multiplexer #(.width(32)) multiplexer_2 (
    .in0(MemAddr), .in1(DataOutput), .out(multiplexer_2_out), .sel(write));  // open: en
  EXTmodule_1 extmodule_1_1 (.EXTop(EXTop), .imm16(imm16), .Output(EXT32));  // open: imm26
  GRFmodule_1 grfmodule_1_1 (
    .rs_5(rs), .rt_5(rt), .rd_5(multiplexer_1_out), .WD(multiplexer_2_out), .RD1(RD1), .RD2(MemData),
    .clk(clk), .reset(reset), .GRFop(RegWrite));
  Multiplexer #(.width(32)) multiplexer_3 (
    .in0(MemData), .in1(EXT32), .out(multiplexer_3_out), .sel(IMMop));  // open: en
  ALUmodule_1 alumodule_1_1 (.ALUop(ALUop), .memory_rs(RD1), .memory_rt(multiplexer_3_out), .ANS(MemAddr), .zero(zero));
  DMmodule_1 dmmodule_1_1 (
    .DMop(MemWrite), .address(MemAddr), .DataInput(MemData), .clk(clk), .reset(reset), .DataOutput(DataOutput));
  Multiplexer #(.width(5)) multiplexer_4 (.in0(rt), .in1(rd), .out(RegAddr), .sel(AddSub));  // open: en
  Multiplexer #(.width(32)) multiplexer_5 (.in0(MemAddr), .in1(DataOutput), .out(RegData), .sel(write));  // open: en

  // Other names for the same wires on the sheet: ANS[31:0] = MemAddr; currentPC[31:0] = PC; DMop = MemWrite;
  //   GRFop = RegWrite; instruction[31:0] = Instr; RD2[31:0] = MemData

  // Notes on the sheet:
  //   Input
  //   CPU
  //   Output
endmodule
